# Fritzing sketch circuit (saved by Fritzing 0.7.12b)
breadboards: 2

parts:
  Arduino_Ethernet_Shield1 = Arduino Ethernet Shield
  R1 = Resistor [tolerance=±5% resistance=10k package=THT]
  T1 = LM35 Temperature Sensor [package="TO92 [THT]"]
  R2 = Photocell (LDR) [package=THT]

nets:
  N1: Arduino_Ethernet_Shield1.D3, R1.Pin_0
  N2: Arduino_Ethernet_Shield1.+5V, T1.+Vs
  GND: Arduino_Ethernet_Shield1.GND, T1.GND
  N3: Arduino_Ethernet_Shield1.A0, T1.Vout
  N4: Arduino_Ethernet_Shield1.A1, R2.pin_1
  N5: Arduino_Ethernet_Shield1.A2, R1.Pin_1
